# Fritzing sketch Testing-setup (saved by Fritzing 0.9.2b)
circuit board: 8.47431cm x 8.86055cm
breadboards: 1

parts:
  Onderdeel1 = Arduino Uno (Rev3)
  R1 = Resistor [tolerance=±5% resistance=220 package=THT]
  R2 = Resistor [tolerance=±5% resistance=220 package=THT]
  R3 = Resistor [tolerance=±5% resistance=220 package=THT]
  R4 = Resistor [tolerance=±5% resistance=220 package=THT]
  LED1 = LED - 5mm [color="Red (633nm)" package="5 mm [THT]"]
  LED2 = LED - 5mm [color="Yellow (592nm)" package="5 mm [THT]"]
  LED3 = LED - 5mm [color="Yellow (592nm)" package="5 mm [THT]"]
  LED4 = LED - 5mm [color="Green (565nm)" package="5 mm [THT]"]
  S1 = Pushbutton [package="[THT]"]
  S2 = Pushbutton [package="[THT]"]
  R5 = Resistor [tolerance=±5% resistance=10k package=THT]
  R6 = Resistor [tolerance=±5% resistance=10k package=THT]
  J1 = Piezo Speaker
  J2 = Basic Servo

nets:
  N1: Onderdeel1.D8, J1.pin2
  N2: Onderdeel1.D9_PWM, S2.Pin_3, S2.Pin_4, R5.Pin_0
  GND: Onderdeel1.GND, R1.Pin_1, R2.Pin_1, R3.Pin_1, R4.Pin_1, R5.Pin_1, R6.Pin_1, J1.pin1, J2.gnd
  N3: Onderdeel1.D2, S1.Pin_1, S1.Pin_2, R6.Pin_0
  N4: Onderdeel1.D3_PWM, LED1.anode
  N5: Onderdeel1.D4, LED2.anode
  N6: Onderdeel1.D5_PWM, LED3.anode
  N7: Onderdeel1.D6_PWM, LED4.anode
  N8: Onderdeel1.D7, J2.pulse
  5V: Onderdeel1.5V, S1.Pin_3, S1.Pin_4, S2.Pin_1, S2.Pin_2, J2.vcc
  N9: R1.Pin_0, LED4.cathode
  N10: R2.Pin_0, LED3.cathode
  N11: R3.Pin_0, LED2.cathode
  N12: R4.Pin_0, LED1.cathode

// code stored in the sketch: Light.ino
void resetLights(){
	digitalWrite(3, LOW);
	digitalWrite(4, LOW);
	digitalWrite(5, LOW);
	digitalWrite(6, LOW);
}

void allLights(){
	digitalWrite(3, HIGH);
	digitalWrite(4, HIGH);
	digitalWrite(5, HIGH);
	digitalWrite(6, HIGH);
}

// code stored in the sketch: SerialOut.ino
void SerialOut(int msg){
	switch (msg)
	{
	case 0:
		Serial.println("OK RIDERS RANDOM START");
		break;
	case 1:
		Serial.println("RIDERS READY - WATCH THE GATE");
		break;
	case 2:
		Serial.println("GATE DOWN");
		break;
	case 3:
		Serial.println("STOP");
		break;
	default:
		break;
	}
}

// code stored in the sketch: Sketch.ino
#include <Servo.h>

int switchState = 0;
int resetState = 0;
int pulseFreq = 632;
Servo gate;

void setup(){
	pinMode(3, OUTPUT); //Light1 - RED
	pinMode(4, OUTPUT); //Light2 - YELLOW
	pinMode(5, OUTPUT); //Light3 - YELLOW
	pinMode(6, OUTPUT); //Light4 - GREEN
	pinMode(2, INPUT);  //Start Button
	pinMode(9, INPUT);  //Reset Button
	gate.attach(7);
	Serial.begin(9600);
}

void loop(){
	while (1)
	{
		interrupts();
		switchState = digitalRead(2);
		resetState = digitalRead(9);
		int inVal = 0;
		if (Serial.available() > 0){
			inVal = Serial.read() - '0';
		}

		if (resetState == HIGH || inVal == 1){
			inVal = 0;
			gate.write(165);
			resetLights();
		}
		else if (switchState == HIGH || inVal == 2){
			inVal = 0;
			resetLights();
			SerialOut(0);
			delay(1800);

			SerialOut(1);
			delay(2700);
			float randomTime = random(100, 2700);
			delay(randomTime);
			Serial.println(2.7 + randomTime / 1000);

			digitalWrite(3, HIGH);
			tone(8, pulseFreq, 600);
			testStop();

			delay(1200);
			digitalWrite(4, HIGH);
			tone(8, pulseFreq, 600);
			testStop();

			delay(1200);
			digitalWrite(5, HIGH);
			tone(8, pulseFreq, 600);
			testStop();

			delay(1200);
			allLights();
			tone(8, pulseFreq, 2250);
			delay(2250);
			SerialOut(2);
			gate.write(120);
			delay(5000);
		}

	}
}

// code stored in the sketch: Stop.ino
void testStop(){
	resetState = digitalRead(9);
	if (resetState == HIGH)
	{
		SerialOut(3);
		for (int i = 0; i < 3; i++){
			tone(8, pulseFreq, 600);
			allLights();
			delay(400);
			resetLights();
			delay(400);
		}

		while (true) loop();
	}
}
